# Fritzing sketch shield_gsm (saved by Fritzing 0.9.2b)
breadboards: 1

parts:
  Componente1 = Arduino Uno (Rev3)  # not connected
  PIR1 = PIR sensor
  Componente2 = Arduino GSM Shield
  LED1 = LED - 5mm [color="Red (633nm)" package="5 mm [THT]"]  # not connected
  R1 = Resistor [tolerance=±5% resistance=10k package=THT]
  R2 = Photocell (LDR) [package=THT]

nets:
  VDD: PIR1.VDD, Componente2.5V, R1.Pin_1
  N1: PIR1.SIG, Componente2.PWM_D4
  N2: PIR1.GND, Componente2.AGND, R2.pin_0
  N3: Componente2.A0, R1.Pin_0, R2.pin_1
